// Logisim project ede.circ as structural Verilog: 1 circuit, main circuit main
module main (
  input  in_1,
  input  in_2,
  input  in_3,
  input  in_4,
  input  in_5,
  output out_6,
  output out_7,
  output out_8,
  output out_9
);

  wire and_1_out, and_2_out, and_3_out, and_4_out, clock_1_out, clock_2_out, d_ff_1_q, d_ff_1_qn, d_ff_2_q,
       d_ff_2_qn, d_ff_4_qn, not_1_out, not_2_out, or_1_out, or_2_out, xnor_1_out, xor_1_out;

  not not_1 (not_1_out, in_3);
  not not_2 (not_2_out, in_4);
  xor xor_1 (xor_1_out, out_6, out_7);
  buf and_1 (and_1_out, not_1_out);  // AND_Gate
  // AND_Gate and_2 has open pins: out=and_2_out
  buf and_3 (and_3_out, in_4);  // AND_Gate
  buf and_4 (and_4_out, not_2_out);  // AND_Gate
  Clock clock_1 (.out(clock_1_out));
  or or_1 (or_1_out, and_1_out, and_2_out);
  or or_2 (or_2_out, and_3_out, and_4_out);
  Clock clock_2 (.out(clock_2_out));
  xnor xnor_1 (xnor_1_out, xor_1_out, in_2);
  D_Flip_Flop d_ff_1 (.clk(clock_1_out), .D(or_1_out), .Q(d_ff_1_q), .Qn(d_ff_1_qn), .reset(in_5));  // open: preset, en
  D_Flip_Flop d_ff_2 (.clk(clock_1_out), .D(or_2_out), .Q(d_ff_2_q), .Qn(d_ff_2_qn), .reset(in_5));  // open: preset, en
  D_Flip_Flop d_ff_3 (.clk(clock_2_out), .D(xnor_1_out), .Q(out_6), .reset(in_1));  // open: Qn, preset, en
  D_Flip_Flop d_ff_4 (.clk(clock_2_out), .D(d_ff_4_qn), .Q(out_7), .Qn(d_ff_4_qn), .reset(in_1));  // open: preset, en
  buf and_5 (out_8, d_ff_1_q);  // AND_Gate
  and and_6 (out_9, d_ff_1_qn, d_ff_2_q);
  Hex_Digit_Display hex_digit_display_1 (.value({2'b00, out_6, out_7}));  // open: dp
endmodule
